// Logisim project a2p2_starter.circ as structural Verilog: 1 circuit, main circuit main
module main (
  input  A,
  input  B,
  input  C,
  input  D,
  output W,
  output X
);

  wire and_1_out, and_2_out, and_3_out, and_4_out, and_5_out, and_6_out, not_1_out, not_2_out, not_3_out,
       not_4_out;

  not not_1 (not_1_out, A);
  not not_2 (not_2_out, B);
  not not_3 (not_3_out, C);
  not not_4 (not_4_out, D);
  and and_1 (and_1_out, A, C);
  and and_2 (and_2_out, B, C);
  and and_3 (and_3_out, B, D);
  and and_4 (and_4_out, not_2_out, not_4_out);
  and and_5 (and_5_out, not_1_out, not_3_out);
  and and_6 (and_6_out, not_2_out, not_3_out);
  or or_1 (W, and_6_out, and_5_out, and_4_out);
  or or_2 (X, and_3_out, and_2_out, and_1_out);

  // Notes on the sheet:
  //   Inputs
  //   Outputs
endmodule
