// Logisim project sle2_starter.circ as structural Verilog: 1 circuit, main circuit main
module main (
  input  in_1,
  output Output
);

  wire and_1_out, and_2_out, and_3_out, and_4_out, clock_1_out, d_ff_1_q, d_ff_2_q, d_ff_2_qn, or_1_out,
       or_2_out;

  Clock clock_1 (.out(clock_1_out));
  or or_1 (or_1_out, and_2_out, and_1_out);
  or or_2 (or_2_out, and_3_out, and_4_out);
  D_Flip_Flop #(.trigger("falling")) d_ff_1 (
    .clk(clock_1_out), .D(or_1_out), .Q(d_ff_1_q));  // open: Qn, preset, en, reset
  D_Flip_Flop #(.trigger("falling")) d_ff_2 (
    .clk(clock_1_out), .D(or_2_out), .Q(d_ff_2_q), .Qn(d_ff_2_qn));  // open: preset, en, reset
  and and_1 (and_1_out, d_ff_1_q, in_1);
  and and_2 (and_2_out, d_ff_2_q, in_1);
  and and_3 (and_3_out, in_1, d_ff_2_qn);
  and and_4 (and_4_out, d_ff_1_q, in_1);
  and and_5 (Output, d_ff_1_q, d_ff_2_q);

  // Notes on the sheet:
  //   Input
endmodule
